# Fritzing sketch samogon (saved by Fritzing 0.9.4)

parts:
  U1 = ESP8266 ESP-01 Upgraded WiFi Module [part_number=ESP8266]
  DS18B20 = DS18B20 1-Wire Temperature Sensor
  R1 = Resistor [tolerance=±5% resistance=4.7k package=THT]
  LD1117V33 = Voltage Regulator - 5V [package="TO220 [THT]"]
  C1 = Ceramic Capacitor [capacitance=100nF package="100 mil [THT, multilayer]"]
  C2 = Electrolytic Capacitor [capacitance=10µF package="100 mil [THT, electrolytic]"]

nets:
  VCC: U1.VCC, DS18B20.VDD, R1.Pin_1
  N1: U1.GPIO_2, DS18B20.DQ, R1.Pin_0
  GND: U1.GND, DS18B20.GND
  N2: LD1117V33.GND, C2.+
  N3: LD1117V33.output_voltage, C1.1
  N4: C1.0, C2.-

notes:
  +5v

custom parts:
  ESP8266 ESP-01 Upgraded WiFi Module: Upgraded Version ESP-01,all Flash are upgraded to 1M byte.Also support Cloud service remote transmission.
